# Fritzing sketch Wekker (saved by Fritzing 0.7.12b)

parts:
  Arduino1 = Arduino
  Grote_rode_knop = Round Pushbutton  # not connected
  Settings = Round Pushbutton  # not connected
  Draaiknop = Rotary Encoder [package=THT]
  Klok = Real Time Clock Module - DS1307 RTC Breakout Board
  Wekker_aan/uit = Tilt Switch [package=THT]  # not connected
  Radio_aan/uit = Tilt Switch [package=THT]  # not connected
  Display = atmega328 [package=dip]
  U2 = mystery part, 5 pins [chip_label=KIT-10733]

nets:
  GND: Arduino1.GND, Draaiknop.EncoderPinC, Klok.GND, Display.GND, U2.pin1
  +5V: Arduino1.+5V, Klok.5V, Display.VCC, U2.pin3
  N1: Arduino1.A4, Klok.SDA
  N2: Arduino1.A5, Klok.SCL
